# Fritzing sketch butia shield 5b (saved by Fritzing 0.3.19b)
breadboards: 1

parts:
  U1 = Arduino Mega
  AX-12 = female pin header, 3 pins [form="♀ (female)"]
  R15 = Resistor [resistance=22k package=THT]
  R13 = Resistor [resistance=22k package=THT]
  R14 = Resistor [resistance=22k package=THT]
  R16 = Resistor [resistance=22k package=THT]
  R12 = Resistor [resistance=22k package=THT]
  R11 = Resistor [resistance=22k package=THT]
  R9 = Resistor [resistance=22k package=THT]
  R10 = Resistor [resistance=22k package=THT]
  R5 = Resistor [resistance=22k package=THT]
  R4 = Resistor [resistance=22k package=THT]
  R1 = Resistor [resistance=22k package=THT]
  R2 = Resistor [resistance=22k package=THT]
  R6 = Resistor [resistance=22k package=THT]
  R7 = Resistor [resistance=22k package=THT]
  R8 = Resistor [resistance=22k package=THT]
  R3 = Resistor [resistance=22k package=THT]
  motores = screw terminal, 6 pins
  L293D = L293D
  R17 = Resistor [resistance=6.8k package=THT]
  R18 = Resistor [resistance=6.8k package=THT]
  conector_0 = Conector de 9 pines butiá (version 4) [form="♀ (female)"]
  conector_1 = Conector de 9 pines butiá (version 4) [form="♀ (female)"]
  conector_2 = Conector de 9 pines butiá (version 4) [form="♀ (female)"]
  conector_3 = Conector de 9 pines butiá (version 4) [form="♀ (female)"]
  conector_4 = Conector de 9 pines butiá (version 4) [form="♀ (female)"]
  conector_6 = Conector de 9 pines butiá (version 4) [form="♀ (female)"]
  conector_7 = Conector de 9 pines butiá (version 4) [form="♀ (female)"]
  conector_5 = Conector de 9 pines butiá (version 4) [form="♀ (female)"]

nets:
  GND: U1.GND, AX-12.pin1, motores.pin6, L293D.connector3, L293D.connector4, L293D.connector11, L293D.connector12, conector_0.connector0, conector_1.connector0, conector_2.connector0, conector_3.connector0, conector_4.connector0, conector_6.connector0, conector_7.connector0, conector_5.connector0
  N1: U1.D11, conector_7.connector3
  N2: U1.D10, conector_6.connector3
  N3: U1.D9, conector_5.connector3
  N4: U1.D8, conector_4.connector3
  N5: U1.D7, conector_3.connector3
  N6: U1.D6, conector_2.connector3
  N7: U1.D5, conector_1.connector3
  N8: U1.D4, conector_0.connector3
  N9: U1.D3, L293D.connector8
  N10: U1.D2, L293D.connector0
  N11: U1.+5V, R15.Pin_0, R13.Pin_0, R14.Pin_0, R16.Pin_0, R12.Pin_0, R11.Pin_0, R9.Pin_0, R10.Pin_0, R5.Pin_0, R4.Pin_0, R1.Pin_0, R2.Pin_0, R6.Pin_0, R7.Pin_0, R8.Pin_0, R3.Pin_0, L293D.connector15, R17.Pin_1, R18.Pin_1, conector_0.connector5, conector_1.connector5, conector_2.connector5, conector_3.connector5, conector_4.connector5, conector_6.connector5, conector_7.connector5, conector_5.connector5
  N12: U1.VIN, AX-12.pin2, motores.pin1, L293D.connector7
  N13: U1.A0, conector_0.connector6
  N14: U1.A1, conector_1.connector6
  N15: U1.A2, conector_2.connector6
  N16: U1.A3, conector_3.connector6
  N17: U1.A4, conector_4.connector6
  N18: U1.A5, conector_5.connector6
  N19: U1.D18, U1.D19, AX-12.pin3
  N20: U1.D20, R17.Pin_0, conector_0.connector7, conector_1.connector7, conector_2.connector7, conector_3.connector7, conector_4.connector7, conector_6.connector7, conector_7.connector7, conector_5.connector7
  N21: U1.D21, R18.Pin_0, conector_0.connector8, conector_1.connector8, conector_2.connector8, conector_3.connector8, conector_4.connector8, conector_6.connector8, conector_7.connector8, conector_5.connector8
  N22: U1.D22, L293D.connector6
  N23: U1.D23, L293D.connector1
  N24: U1.D24, L293D.connector14
  N25: U1.D25, L293D.connector9
  N26: U1.D26, conector_7.connector4
  N27: U1.D27, conector_6.connector4
  N28: U1.D28, conector_5.connector4
  N29: U1.D29, conector_4.connector4
  N30: U1.D30, conector_3.connector4
  N31: U1.D31, conector_2.connector4
  N32: U1.D32, conector_1.connector4
  N33: U1.D33, conector_0.connector4
  N34: U1.D34, R16.Pin_1, conector_7.connector1
  N35: U1.D35, R15.Pin_1, conector_7.connector2
  N36: U1.D36, R14.Pin_1, conector_6.connector1
  N37: U1.D37, R13.Pin_1, conector_6.connector2
  N38: U1.D38, R12.Pin_1, conector_5.connector1
  N39: U1.D39, R11.Pin_1, conector_5.connector2
  N40: U1.D40, R10.Pin_1, conector_4.connector1
  N41: U1.D41, R9.Pin_1, conector_4.connector2
  N42: U1.D42, R8.Pin_1, conector_3.connector1
  N43: U1.D43, R7.Pin_1, conector_3.connector2
  N44: U1.D44, R6.Pin_1, conector_2.connector1
  N45: U1.D45, R5.Pin_1, conector_2.connector2
  N46: U1.D46, R4.Pin_1, conector_1.connector1
  N47: U1.D47, R3.Pin_1, conector_1.connector2
  N48: U1.D48, R2.Pin_1, conector_0.connector1
  N49: U1.D49, R1.Pin_1, conector_0.connector2
  N50: U1.A6, conector_6.connector6
  N51: U1.A7, conector_7.connector6
  N52: motores.pin2, L293D.connector10
  N53: motores.pin3, L293D.connector13
  N54: motores.pin4, L293D.connector2
  N55: motores.pin5, L293D.connector5

notes:
  1
